# Fritzing sketch CircuitSchematic (saved by Fritzing 0.7.0b)
breadboards: 1

parts:
  Nano1 = Arduino Nano v2.3
  U1 = mystery part, 3 pins [chip_label=LCD spacing=300mil]
  DC_Power1 = DC Power [voltage=5]
  U2 = mystery part, 3 pins [chip_label=ENC spacing=300mil]
  IC1 = Hex Inverter Schmitt Trigger SN74HC14 [package="DIP (Dual Inline)"]
  1_Blue = LED - 5mm [color="White (4500K)" package="5 mm [THT]"]
  R1 = Resistor [tolerance=±5% resistance=81k package=THT]
  2_Green = LED - 5mm [color="White (4500K)" package="5 mm [THT]"]
  R2 = Resistor [tolerance=±5% resistance=100k package=THT]
  3_Orange = LED - 5mm [color="White (4500K)" package="5 mm [THT]"]
  R3 = Resistor [tolerance=±5% resistance=4.7k package=THT]
  4_Purple = LED - 5mm [color="White (4500K)" package="5 mm [THT]"]
  R4 = Resistor [tolerance=±5% resistance=2.7k package=THT]
  U3 = mystery part, 5 pins [chip_label=LEDSW spacing=300mil]
  SSR1 = SSR [package=THT]
  SSR2 = SSR [package=THT]
  C1 = Electrolytic Capacitor [capacitance=10µF voltage=25V package="100 mil [THT, electrolytic]"]
  C2 = Electrolytic Capacitor [capacitance=10µF voltage=25V package="100 mil [THT, electrolytic]"]
  R5 = Resistor [tolerance=±5% resistance=8k package=THT]
  R6 = Resistor [tolerance=±5% resistance=8k package=THT]
  CTL_IN = Stereo Jack (TRS) 3.5mm [package="PG203J [THT]"]
  S1 = Round Pushbutton
  OUT3 = Stereo Jack (TRS) 3.5mm [package="PG203J [THT]"]
  MIDIOUT = Stereo Jack (TRS) 3.5mm [package="PG203J [THT]"]
  OUT1 = Stereo Jack (TRS) 3.5mm [package="PG203J [THT]"]
  OUT2 = Stereo Jack (TRS) 3.5mm [package="PG203J [THT]"]
  R7 = Resistor [tolerance=±5% resistance=220 package=THT]
  R8 = Resistor [tolerance=±5% resistance=220 package=THT]
  R9 = Resistor [tolerance=±5% resistance=380 package=THT]
  R11 = Resistor [tolerance=±5% resistance=380 package=THT]
  R12 = Resistor [tolerance=±5% resistance=380 package=THT]
  R10 = Resistor [tolerance=±5% resistance=380 package=THT]
  R13 = Resistor [tolerance=±5% resistance=4.7k package=THT]
  R14 = Resistor [tolerance=±5% resistance=4.7k package=THT]
  R15 = Resistor [tolerance=±5% resistance=5.6k package=THT]
  R16 = Resistor [tolerance=±5% resistance=10k package=THT]

nets:
  N1: Nano1.GND, DC_Power1.V+, U2.pin3, R16.Pin_1
  N2: Nano1.D2, U2.pin2
  N3: Nano1.D3, U2.pin1
  N4: Nano1.D4, U3.pin5, R16.Pin_0
  N5: Nano1.D5, R14.Pin_1
  N6: Nano1.D6, R13.Pin_1
  N7: Nano1.D7, IC1.6A
  N8: Nano1.D8, 4_Purple.anode
  N9: Nano1.D9, 3_Orange.anode
  N10: Nano1.D10, 2_Green.anode
  N11: Nano1.D11, R15.Pin_1
  N12: Nano1.D12, 1_Blue.anode
  N13: Nano1.A6, IC1.4A
  N14: Nano1.A5, U1.pin3
  N15: Nano1.A4, R8.Pin_0
  N16: Nano1.A3, SSR2.A0
  N17: Nano1.A2, SSR2.A2
  N18: Nano1.A1, SSR1.A0
  N19: Nano1.A0, SSR1.A2
  +5V: Nano1.+5V, U1.pin2, IC1.VCC, U3.pin1, R5.Pin_1, R6.Pin_1, R7.Pin_0
  9V: Nano1.VIN
  N20: U1.pin1, IC1.GND, R1.Pin_1, R2.Pin_1, R3.Pin_1, R4.Pin_1, C1.-, C2.-, CTL_IN.Sleeve, S1.leg1, MIDIOUT.Sleeve, R9.Pin_0, R11.Pin_0, R12.Pin_0, R10.Pin_0
  N21: IC1.4Y, C1.+, R6.Pin_0, CTL_IN.Tip
  N22: IC1.6Y, C2.+, R5.Pin_0, S1.leg0
  N23: 1_Blue.cathode, R1.Pin_0
  N24: 2_Green.cathode, R2.Pin_0
  N25: 3_Orange.cathode, R3.Pin_0
  N26: 4_Purple.cathode, R4.Pin_0
  N27: U3.pin2, R13.Pin_0
  N28: U3.pin3, R14.Pin_0
  N29: U3.pin4, R15.Pin_0
  N30: SSR1.A1, R9.Pin_1
  N31: SSR1.In_1_Ground, R12.Pin_1
  N32: SSR1.SDA_-_I2C_Data, OUT3.Sleeve
  N33: SSR1.SCL_-_I2C_Clock, OUT3.Tip
  N34: SSR1.WP_-_Write_Protect, OUT2.Sleeve
  N35: SSR1.+V, OUT2.Tip
  N36: SSR2.A1, R11.Pin_1
  N37: SSR2.In_1_Ground, R10.Pin_1
  N38: SSR2.SDA_-_I2C_Data, OUT1.Sleeve
  N39: SSR2.SCL_-_I2C_Clock, OUT1.Tip
  N40: MIDIOUT.Ring, R7.Pin_1
  N41: MIDIOUT.Tip, R8.Pin_1

custom parts:
  SSR: SSR Relay
